// Logisim project model.circ as structural Verilog: 2 circuits, main circuit main
module main (
);

  wire and_1_out, and_2_out, and_3_out, and_4_out, and_5_out, and_6_out, and_7_out, counter_1_carry,
       decoder_1_out0, decoder_1_out1, decoder_1_out2, decoder_1_out3, nor_1_out, not_1_out, not_2_out,
       not_5_out, not_6_out, phi2, pull_resistor_1_node, pull_resistor_2_node, pull_resistor_3_node,
       pull_resistor_4_node, RESET_out, w65c02s_expert_1_p1, w65c02s_expert_1_p7, w65c02s_expert_1_p8,
       w65c02s_expert_1_p9, w65c02s_expert_1_p15, w65c02s_expert_1_p17, w65c02s_expert_1_p18;
  wire [3:0] w65c02s_expert_1_p19, w65c02s_expert_1_p19_2;
  wire [3:2] w65c02s_expert_1_p20;
  wire [7:0] BankNum, BankSel0, BankSel1, BankSel2, StatusOut, transistor_1_out, undriven;
  wire [13:0] w65c02s_expert_1_p20_2;

  Button RESET (.out(RESET_out));
  Clock clock_1 (.out(phi2));
  nor nor_1 (nor_1_out, phi2, counter_1_carry);
  Counter #(.max('h7), .width(3)) counter_1 (
    .load(1'b0), .count(1'b1), .carry(counter_1_carry), .up(1'b1), .clk(nor_1_out), .clr(RESET_out));  // open: D, Q
  not not_1 (not_1_out, counter_1_carry);
  LED OpCodeSync (.in(w65c02s_expert_1_p7));
  LED VectorPull (.in(not_2_out));
  not not_2 (not_2_out, pull_resistor_1_node);
  Pull_Resistor #(.pull(1)) pull_resistor_1 (.node(pull_resistor_1_node));
  Pull_Resistor #(.pull(1)) pull_resistor_2 (.node(pull_resistor_2_node));
  Pull_Resistor #(.pull(1)) pull_resistor_3 (.node(pull_resistor_3_node));
  Pull_Resistor #(.pull(1)) pull_resistor_4 (.node(pull_resistor_4_node));
  Hex_Digit_Display hex_digit_display_1 (.value(w65c02s_expert_1_p19_2));  // open: dp
  Hex_Digit_Display hex_digit_display_2 (.value({w65c02s_expert_1_p20, w65c02s_expert_1_p20_2[13:12]}));  // open: dp
  // W65C02S__Expert w65c02s_expert_1: pin names not known; wires that end beside it: w65c02s_expert_1_p1, pull_resistor_1_node, pull_resistor_2_node, pull_resistor_3_node, w65c02s_expert_1_p1, pull_resistor_4_node, w65c02s_expert_1_p7, w65c02s_expert_1_p8, w65c02s_expert_1_p9, w65c02s_expert_1_p8, w65c02s_expert_1_p9, w65c02s_expert_1_p9, w65c02s_expert_1_p9, not_1_out, w65c02s_expert_1_p15, phi2, w65c02s_expert_1_p17, w65c02s_expert_1_p18, {w65c02s_expert_1_p19_2, w65c02s_expert_1_p19}, {w65c02s_expert_1_p20, w65c02s_expert_1_p20_2}
  Hex_Digit_Display hex_digit_display_3 (.value(w65c02s_expert_1_p19));  // open: dp
  Hex_Digit_Display hex_digit_display_4 (.value(w65c02s_expert_1_p20_2[11:8]));  // open: dp
  Hex_Digit_Display hex_digit_display_5 (.value(w65c02s_expert_1_p20_2[7:4]));  // open: dp
  not not_3 (w65c02s_expert_1_p8, w65c02s_expert_1_p18);
  Hex_Digit_Display hex_digit_display_6 (.value(w65c02s_expert_1_p20_2[3:0]));  // open: dp
  not not_4 (w65c02s_expert_1_p9, w65c02s_expert_1_p18);
  Pull_Resistor #(.pull(1)) pull_resistor_5 (.node(not_1_out));
  Pull_Resistor #(.pull(1)) pull_resistor_6 (.node(w65c02s_expert_1_p15));
  Pull_Resistor #(.pull(1)) pull_resistor_7 (.node(w65c02s_expert_1_p17));
  // NoConnect on undriven
  Multiplexer #(.select(2), .width(8)) multiplexer_1 (
    .in0(BankSel0), .in1(BankSel1), .in2(BankSel2), .in3(undriven), .out(BankNum), .sel(w65c02s_expert_1_p20));
  LED led_1 (.in(and_1_out));
  and and_1 (and_1_out, w65c02s_expert_1_p20[2], w65c02s_expert_1_p20[3]);
  CY7C1041DV33 Bank0 (
    .OE(w65c02s_expert_1_p18), .WE(w65c02s_expert_1_p18), .BHE(w65c02s_expert_1_p20_2[0]), .BLE(not_5_out),
    .addr_in({{5{1'b0}}, w65c02s_expert_1_p20_2[13:1]}), .CE(1'b0),
    .DQ2({w65c02s_expert_1_p19_2, w65c02s_expert_1_p19}), .DQ1({w65c02s_expert_1_p19_2, w65c02s_expert_1_p19}));
  not not_5 (not_5_out, w65c02s_expert_1_p20_2[0]);
  not not_6 (not_6_out, w65c02s_expert_1_p18);
  Decoder #(.select(3)) decoder_1 (
    .out0(decoder_1_out0), .out1(decoder_1_out1), .out2(decoder_1_out2), .out3(decoder_1_out3),
    .sel(w65c02s_expert_1_p20_2[2:0]), .en(and_3_out));  // open: out4, out5, out6, out7
  and and_2 (and_2_out, w65c02s_expert_1_p20_2[3], w65c02s_expert_1_p20_2[4], w65c02s_expert_1_p20_2[5], w65c02s_expert_1_p20_2[6], w65c02s_expert_1_p20_2[7], w65c02s_expert_1_p20_2[8], w65c02s_expert_1_p20_2[9], w65c02s_expert_1_p20_2[10]);
  and and_3 (and_3_out, and_2_out, w65c02s_expert_1_p20_2[11], w65c02s_expert_1_p20_2[11], w65c02s_expert_1_p20_2[11], w65c02s_expert_1_p20_2[12], w65c02s_expert_1_p20_2[12], w65c02s_expert_1_p20_2[13], and_1_out);
  assign {w65c02s_expert_1_p19_2, w65c02s_expert_1_p19} = w65c02s_expert_1_p18 ? transistor_1_out : 8'bz;  // Controlled_Buffer controlled_buffer_1
  and and_4 (and_4_out, decoder_1_out0, not_6_out);
  and and_5 (and_5_out, decoder_1_out1, not_6_out);
  and and_6 (and_6_out, decoder_1_out2, not_6_out);
  and and_7 (and_7_out, decoder_1_out3, not_6_out);
  Register BankNum0 (
    .D({w65c02s_expert_1_p19_2, w65c02s_expert_1_p19}), .en(and_4_out), .clk(phi2), .Q(BankSel0), .clr(1'b0));
  Register BankNum1 (
    .D({w65c02s_expert_1_p19_2, w65c02s_expert_1_p19}), .en(and_5_out), .clk(phi2), .Q(BankSel1), .clr(1'b0));
  Register BankNum2 (
    .D({w65c02s_expert_1_p19_2, w65c02s_expert_1_p19}), .en(and_6_out), .clk(phi2), .Q(BankSel2), .clr(1'b0));
  Register HWStatus (
    .D({w65c02s_expert_1_p19_2, w65c02s_expert_1_p19}), .en(and_7_out), .clk(phi2), .Q(StatusOut), .clr(1'b0));
  Transistor #(.width(8)) transistor_1 (.in(BankSel0), .out(transistor_1_out), .gate(decoder_1_out0));
  Transistor #(.width(8)) transistor_2 (.in(BankSel1), .out(transistor_1_out), .gate(decoder_1_out1));
  Transistor #(.width(8)) transistor_3 (.in(BankSel2), .out(transistor_1_out), .gate(decoder_1_out2));
  Transistor #(.width(8)) transistor_4 (.in(StatusOut), .out(transistor_1_out), .gate(decoder_1_out3));

  // Notes on the sheet:
  //   CLOCK
  //   RESET
  //   DATA
  //   ADDR
  //   CPU
  //   VPN (of 16k pages)
  //   LS bits
  //   Big pin count
  //   BANKED PAGES
  //   RAM BANKS
  //   Fixed (kernel, himem) pg
  //   Fixed pg addr decode
  //   rw
  //   FIXED PAGE & REGISTERS
  //   cs0
  //   cs1
  //   cs2
  //   cs3
  //   RAM BANK SELECTION
  //   MACHINE STATUS
endmodule

module CY7C1041DV33 (
  input  CE,
  input  [17:0] addr_in,
  input  BHE,
  input  BLE,
  input  OE,
  input  WE,
  input  [7:0] DQ2,
  output [7:0] DQ1
);

  wire buffer_1_out, buffer_2_out, not_1_out, not_2_out, not_3_out;
  wire [7:0] controlled_buffer_1_out, controlled_buffer_2_out, controlled_buffer_3_out, ram_internal_dout;
  wire [18:18] transistor_1_out;

  Transistor transistor_1 (.in(BHE), .out(transistor_1_out[18]), .gate(BLE));
  Pull_Resistor #(.pull(1)) pull_resistor_1 (.node(transistor_1_out[18]));
  not not_1 (not_1_out, OE);
  buf buffer_1 (buffer_1_out, not_2_out);
  not not_2 (not_2_out, WE);
  buf buffer_2 (buffer_2_out, WE);
  RAM #(.addrWidth(19), .asyncread("true")) ram_internal (
    .addr({transistor_1_out[18], addr_in}), .we(not_2_out), .oe(not_1_out), .clk(buffer_1_out),
    .din(controlled_buffer_1_out), .dout(ram_internal_dout));
  assign controlled_buffer_1_out = not_2_out ? controlled_buffer_2_out : 8'bz;  // Controlled_Buffer controlled_buffer_1
  assign controlled_buffer_2_out = not_3_out ? DQ2 : 8'bz;  // Controlled_Buffer controlled_buffer_2
  not not_3 (not_3_out, CE);
  assign controlled_buffer_3_out = not_3_out ? ram_internal_dout : 8'bz;  // Controlled_Buffer controlled_buffer_3
  assign DQ2 = buffer_2_out ? controlled_buffer_3_out : 8'bz;  // Controlled_Buffer controlled_buffer_4

  assign DQ1 = DQ2;

  // Notes on the sheet:
  //   Little-endian hi/lo bit
  //   Active low
  //   The actual ram is 16 bit, this is to emulate but show nicely in Logisim as 8-bit.
endmodule
